# Fritzing sketch FinalFirstCircuit (saved by Fritzing 0.9.3b)
circuit board: 11.563cm x 8.90701cm
breadboards: 1

parts:
  LED = LED - 5mm [color="Red (633nm)" package="5 mm [THT]"]
  J1 = female pin header, 2 pins [form="♀ (female)"]
  J2 = female pin header, 2 pins [form="♀ (female)"]
  Part1 = Arduino Uno (Rev3)
  J3 = shrouded pin header, 10 pins [form="♂ (shrouded male)"]
  J4 = female pin header, 2 pins [form="♀ (female)"]
  J5 = female pin header, 2 pins [form="♀ (female)"]
  J6 = shrouded pin header, 10 pins [form="♂ (shrouded male)"]
  R1 = Resistor [tolerance=±5% resistance=220 package=THT]

nets:
  N1: LED.cathode, R1.Pin_0
  N2: LED.anode, J1.pin2
  5V: J1.pin1, Part1.5V
  N3: J2.pin1, R1.Pin_1
  GND: J2.pin2, Part1.GND
  N4: Part1.A0, J6.pin1
  N5: Part1.A1, J6.pin2
  N6: Part1.A2, J6.pin3
  N7: Part1.A3, J6.pin4
  N8: Part1.A4/SDA, J6.pin5
  N9: Part1.A5/SCL, J6.pin6
  N10: Part1.D8, J3.pin5
  N11: Part1.D9_PWM, J3.pin6
  N12: Part1.D10_PWM/SS, J3.pin7
  N13: Part1.D11_PWM/MOSI, J3.pin8
  N14: Part1.D12/MISO, J3.pin9
  N15: Part1.D13/SCK, J3.pin10
  N16: Part1.D0/RX, J4.pin2
  N17: Part1.D1/TX, J4.pin1
  N18: Part1.D2, J5.pin1
  N19: Part1.D3_PWM, J5.pin2
  N20: Part1.D4, J3.pin1
  N21: Part1.D5_PWM, J3.pin2
  N22: Part1.D6_PWM, J3.pin3
  N23: Part1.D7, J3.pin4

notes:
  SCNEEL
